// Logisim project 29_Bit_ALU_Parallel.circ as structural Verilog: 12 circuits, main circuit 29bit ALU
module _29bit_ALU (
  input  [1:0] Control,
  input  [28:0] in_2,
  input  [28:0] in_3,
  output [28:0] out_4,
  output [3:0] Flags
);

  wire zero_check_1_output;
  wire [28:0] n29_bit_parallel_adder_1_out_4, n29bit_and_1_out_3, n29bit_or_1_out_3;

  _29bit_AND u_29bit_and_1 (.in_1(in_2), .in_2(in_3), .out_3(n29bit_and_1_out_3));
  _29bit_OR u_29bit_or_1 (.in_1(in_3), .in_2(in_2), .out_3(n29bit_or_1_out_3));
  _29_bit_Parallel_Adder u_29_bit_parallel_adder_1 (
    .in_1(Control[0]), .in_2(in_2), .in_3(in_3), .out_4(n29_bit_parallel_adder_1_out_4), .out_5(Flags[1]),
    .out_6(Flags[0]));
  _4x1_mux u_4x1_mux_1 (
    .in_1(Control), .in_2(n29_bit_parallel_adder_1_out_4), .in_3(n29_bit_parallel_adder_1_out_4),
    .in_4(n29bit_and_1_out_3), .in_5(n29bit_or_1_out_3), .out_6(out_4));
  Negative_Check negative_check_1 (.in_1(out_4), .Output(Flags[3]));
  Zero_Check zero_check_1 (.in_1(out_4), .Output(zero_check_1_output));
  not not_1 (Flags[2], zero_check_1_output);

  // Other names for the same wires on the sheet: Overflow = Flags[0]; Carry = Flags[1]; Zero = Flags[2];
  //   Negative = Flags[3]

  // Notes on the sheet:
  //   29 Bit ALU
  //   0 0 - Adder
  //   0 1 - Subtractor
  //   1 0 - AND
  //   1 1 - OR
  //   Input
  //   A
  //   B
  //   Output
  //   Negative- Zero-Carry-Overflow
  //   Roll - 2207006
endmodule

// AND
module _29bit_AND (
  input  [28:0] in_1,
  input  [28:0] in_2,
  output [28:0] out_3
);

  assign out_3 = in_1 & in_2;  // AND_Gate and_1, 29 bits wide

  // Notes on the sheet:
  //   2207006
  //   A
  //   B
  //   A AND B
endmodule

// OR
module _29bit_OR (
  input  [28:0] in_1,
  input  [28:0] in_2,
  output [28:0] out_3
);

  assign out_3 = in_1 | in_2;  // OR_Gate or_1, 29 bits wide

  // Notes on the sheet:
  //   2207006
  //   A
  //   B
  //   A OR B
endmodule

// Adder
module _1bit_Adder (
  input  Cin,
  input  A,
  input  B,
  output Sum,
  output Cout
);

  wire and_1_out, and_2_out, xor_1_out;

  xor xor_1 (xor_1_out, A, B);
  and and_1 (and_1_out, B, A);
  xor xor_2 (Sum, Cin, xor_1_out);
  and and_2 (and_2_out, Cin, xor_1_out);
  or or_1 (Cout, and_2_out, and_1_out);

  // Notes on the sheet:
  //   2207006
endmodule

// Zero
module Zero_Check (
  input  [28:0] in_1,
  output Output
);

  or or_1 (Output, in_1[0], in_1[1], in_1[2], in_1[3], in_1[4], in_1[5], in_1[6], in_1[7], in_1[8], in_1[9], in_1[10], in_1[11], in_1[12], in_1[13], in_1[14], in_1[15], in_1[16], in_1[17], in_1[18], in_1[19], in_1[20], in_1[21], in_1[22], in_1[23], in_1[24], in_1[25], in_1[26], in_1[27], in_1[28]);

  // Notes on the sheet:
  //   2207006
  //   Input
endmodule

// Neg
module Negative_Check (
  input  [28:0] in_1,
  output Output
);


  assign Output = in_1[28];

  // Notes on the sheet:
  //   2207006
  //   Input
endmodule

module _29bit_CLG (
  input  Cin,
  input  [28:0] in_2,
  input  [28:0] in_3,
  output [28:0] out_4
);

  _4bit_CLG u_4bit_clg_1 (
    .Cin(Cin), .in_2(in_2[3:0]), .in_3(in_3[3:0]), .C1(out_4[0]), .C2(out_4[1]), .C3(out_4[2]), .C4(out_4[3]));
  _4bit_CLG u_4bit_clg_2 (
    .Cin(out_4[3]), .in_2(in_2[7:4]), .in_3(in_3[7:4]), .C1(out_4[4]), .C2(out_4[5]), .C3(out_4[6]),
    .C4(out_4[7]));
  _4bit_CLG u_4bit_clg_3 (
    .Cin(out_4[7]), .in_2(in_2[11:8]), .in_3(in_3[11:8]), .C1(out_4[8]), .C2(out_4[9]), .C3(out_4[10]),
    .C4(out_4[11]));
  _4bit_CLG u_4bit_clg_4 (
    .Cin(out_4[11]), .in_2(in_2[15:12]), .in_3(in_3[15:12]), .C1(out_4[12]), .C2(out_4[13]), .C3(out_4[14]),
    .C4(out_4[15]));
  _4bit_CLG u_4bit_clg_5 (
    .Cin(out_4[15]), .in_2(in_2[19:16]), .in_3(in_3[19:16]), .C1(out_4[16]), .C2(out_4[17]), .C3(out_4[18]),
    .C4(out_4[19]));
  _4bit_CLG u_4bit_clg_6 (
    .Cin(out_4[19]), .in_2(in_2[23:20]), .in_3(in_3[23:20]), .C1(out_4[20]), .C2(out_4[21]), .C3(out_4[22]),
    .C4(out_4[23]));
  _4bit_CLG u_4bit_clg_7 (
    .Cin(out_4[23]), .in_2(in_2[27:24]), .in_3(in_3[27:24]), .C1(out_4[24]), .C2(out_4[25]), .C3(out_4[26]),
    .C4(out_4[27]));
  _1bit_carry u_1bit_carry_1 (.Cin(out_4[27]), .A(in_2[28]), .B(in_3[28]), .Cout(out_4[28]));

  // Notes on the sheet:
  //   A
  //   B
  //   Cout
  //   2207006
endmodule

module _4bit_CLG (
  input  Cin,
  input  [3:0] in_2,
  input  [3:0] in_3,
  output C1,
  output C2,
  output C3,
  output C4
);

  wire and_1_out, and_2_out, and_3_out, and_4_out, and_5_out, and_6_out, and_7_out, and_8_out, and_9_out,
       and_10_out, and_11_out, and_12_out, and_13_out, and_14_out, xor_1_out, xor_2_out, xor_3_out, xor_4_out;

  xor xor_1 (xor_1_out, in_2[0], in_3[0]);
  xor xor_2 (xor_2_out, in_2[1], in_3[1]);
  xor xor_3 (xor_3_out, in_2[2], in_3[2]);
  xor xor_4 (xor_4_out, in_2[3], in_3[3]);
  and and_1 (and_1_out, in_2[0], in_3[0]);
  and and_2 (and_2_out, in_2[1], in_3[1]);
  and and_3 (and_3_out, in_2[2], in_3[2]);
  and and_4 (and_4_out, in_2[3], in_3[3]);
  and and_5 (and_5_out, Cin, xor_1_out);
  and and_6 (and_6_out, Cin, xor_1_out, xor_2_out);
  and and_7 (and_7_out, xor_2_out, and_1_out);
  and and_8 (and_8_out, xor_3_out, xor_2_out, xor_1_out, Cin);
  and and_9 (and_9_out, and_1_out, xor_2_out, xor_3_out);
  and and_10 (and_10_out, xor_3_out, and_2_out);
  and and_11 (and_11_out, xor_4_out, and_3_out);
  and and_12 (and_12_out, xor_4_out, xor_3_out, and_2_out);
  and and_13 (and_13_out, xor_4_out, xor_3_out, xor_2_out, and_1_out);
  and and_14 (and_14_out, xor_4_out, xor_3_out, xor_2_out, xor_1_out, Cin);
  or or_1 (C1, and_5_out, and_1_out);
  or or_2 (C2, and_6_out, and_7_out, and_2_out);
  or or_3 (C3, and_8_out, and_9_out, and_10_out, and_3_out);
  or or_4 (C4, and_14_out, and_13_out, and_12_out, and_11_out, and_4_out);

  // Notes on the sheet:
  //   A
  //   B
  //   2207006
endmodule

// 1bit CLG
module _1bit_carry (
  input  Cin,
  input  A,
  input  B,
  output Cout
);

  wire and_1_out, and_2_out, xor_1_out;

  and and_1 (and_1_out, A, B);
  xor xor_1 (xor_1_out, A, B);
  and and_2 (and_2_out, xor_1_out, Cin);
  or or_1 (Cout, and_1_out, and_2_out);

  // Notes on the sheet:
  //   2207006
endmodule

module _4_bit_Parallel_Adder (
  input  [3:0] in_1,
  input  [3:0] in_2,
  input  [3:0] in_3,
  output [3:0] out_4
);

  _1bit_Adder u_1bit_adder_1 (.Cin(in_1[0]), .A(in_2[0]), .B(in_3[0]), .Sum(out_4[0]));  // open: Cout
  _1bit_Adder u_1bit_adder_2 (.Cin(in_1[1]), .A(in_2[1]), .B(in_3[1]), .Sum(out_4[1]));  // open: Cout
  _1bit_Adder u_1bit_adder_3 (.Cin(in_1[2]), .A(in_2[2]), .B(in_3[2]), .Sum(out_4[2]));  // open: Cout
  _1bit_Adder u_1bit_adder_4 (.Cin(in_1[3]), .A(in_2[3]), .B(in_3[3]), .Sum(out_4[3]));  // open: Cout

  // Notes on the sheet:
  //   2207006
endmodule

// Add-Sub
module _29_bit_Parallel_Adder (
  input  in_1,
  input  [28:0] in_2,
  input  [28:0] in_3,
  output [28:0] out_4,
  output out_5,
  output out_6
);

  wire and_1_out, and_2_out, not_1_out, not_2_out, not_3_out;
  wire [3:0] xor_1_out_2, xor_1_out_3;
  wire [27:0] n29bit_clg_1_out_4;
  wire [28:0] bit_extender_1_out, xor_1_out;

  assign bit_extender_1_out = {{28{in_1}}, in_1};  // Bit_Extender bit_extender_1
  _29bit_CLG u_29bit_clg_1 (
    .Cin(in_1), .in_2(in_2),
    .in_3({xor_1_out[28], xor_1_out_3, xor_1_out[23:20], xor_1_out_2, xor_1_out[15:0]}),
    .out_4({out_5, n29bit_clg_1_out_4}));
  assign {xor_1_out[28], xor_1_out_3, xor_1_out[23:20], xor_1_out_2, xor_1_out[15:0]} = in_3 ^ bit_extender_1_out;  // XOR_Gate xor_1, 29 bits wide
  _4_bit_Parallel_Adder u_4_bit_parallel_adder_1 (
    .in_1({n29bit_clg_1_out_4[2:0], in_1}), .in_2(in_2[3:0]), .in_3(xor_1_out[3:0]), .out_4(out_4[3:0]));
  _4_bit_Parallel_Adder u_4_bit_parallel_adder_2 (
    .in_1(n29bit_clg_1_out_4[6:3]), .in_2(in_2[7:4]), .in_3(xor_1_out[7:4]), .out_4(out_4[7:4]));
  _4_bit_Parallel_Adder u_4_bit_parallel_adder_3 (
    .in_1(n29bit_clg_1_out_4[10:7]), .in_2(in_2[11:8]), .in_3(xor_1_out[11:8]), .out_4(out_4[11:8]));
  _4_bit_Parallel_Adder u_4_bit_parallel_adder_4 (
    .in_1(n29bit_clg_1_out_4[14:11]), .in_2(in_2[15:12]), .in_3(xor_1_out[15:12]), .out_4(out_4[15:12]));
  _4_bit_Parallel_Adder u_4_bit_parallel_adder_5 (
    .in_1(n29bit_clg_1_out_4[18:15]), .in_2(in_2[19:16]), .in_3(xor_1_out_2), .out_4(out_4[19:16]));
  _4_bit_Parallel_Adder u_4_bit_parallel_adder_6 (
    .in_1(n29bit_clg_1_out_4[22:19]), .in_2(in_2[23:20]), .in_3(xor_1_out[23:20]), .out_4(out_4[23:20]));
  _4_bit_Parallel_Adder u_4_bit_parallel_adder_7 (
    .in_1(n29bit_clg_1_out_4[26:23]), .in_2(in_2[27:24]), .in_3(xor_1_out_3), .out_4(out_4[27:24]));
  _1bit_Adder u_1bit_adder_1 (
    .Cin(n29bit_clg_1_out_4[27]), .A(in_2[28]), .B(xor_1_out[28]), .Sum(out_4[28]));  // open: Cout
  not not_1 (not_1_out, in_2[28]);
  not not_2 (not_2_out, xor_1_out[28]);
  and and_1 (and_1_out, not_1_out, not_2_out, out_4[28]);
  not not_3 (not_3_out, out_4[28]);
  and and_2 (and_2_out, not_3_out, in_2[28], xor_1_out[28]);
  or or_1 (out_6, and_1_out, and_2_out);

  // Notes on the sheet:
  //   2207006
  //   A
  //   B
endmodule

// 4x1
module _4x1_mux (
  input  [1:0] in_1,
  input  [28:0] in_2,
  input  [28:0] in_3,
  input  [28:0] in_4,
  input  [28:0] in_5,
  output [28:0] out_6
);

  wire [28:0] and_1_out, and_2_out, and_3_out, and_4_out, bit_extender_1_out, bit_extender_2_out, not_1_out,
       not_2_out, not_3_out, not_4_out;

  assign bit_extender_1_out = {{28{in_1[0]}}, in_1[0]};  // Bit_Extender bit_extender_1
  assign bit_extender_2_out = {{28{in_1[1]}}, in_1[1]};  // Bit_Extender bit_extender_2
  assign not_1_out = ~bit_extender_1_out;  // NOT_Gate not_1, 29 bits wide
  assign not_2_out = ~bit_extender_2_out;  // NOT_Gate not_2, 29 bits wide
  assign not_3_out = ~bit_extender_2_out;  // NOT_Gate not_3, 29 bits wide
  assign not_4_out = ~bit_extender_1_out;  // NOT_Gate not_4, 29 bits wide
  assign and_1_out = not_1_out & not_2_out & in_2;  // AND_Gate and_1, 29 bits wide
  assign and_2_out = bit_extender_1_out & not_3_out & in_3;  // AND_Gate and_2, 29 bits wide
  assign and_3_out = not_4_out & bit_extender_2_out & in_4;  // AND_Gate and_3, 29 bits wide
  assign and_4_out = bit_extender_1_out & bit_extender_2_out & in_5;  // AND_Gate and_4, 29 bits wide
  assign out_6 = and_1_out | and_2_out | and_3_out | and_4_out;  // OR_Gate or_1, 29 bits wide

  // Notes on the sheet:
  //   2207006
endmodule
