// Logisim project 29_Bit_ALU_Serial.circ as structural Verilog: 7 circuits, main circuit main
module main (
  input  [1:0] Control,
  input  [28:0] in_2,
  input  [28:0] in_3,
  output [28:0] out_4,
  output [3:0] Flags
);

  wire zero_check_1_output;
  wire [28:0] n29bit_adder_1_out_4, n29bit_and_1_out_3, n29bit_or_1_out_3;

  _29bit_AND u_29bit_and_1 (.in_1(in_2), .in_2(in_3), .out_3(n29bit_and_1_out_3));
  _29bit_OR u_29bit_or_1 (.in_1(in_3), .in_2(in_2), .out_3(n29bit_or_1_out_3));
  _29bit_Adder u_29bit_adder_1 (
    .in_1(Control[0]), .in_2(in_2), .in_3(in_3), .out_4(n29bit_adder_1_out_4), .out_5(Flags[1]),
    .Overflow(Flags[0]));
  Multiplexer #(.select(2), .width(29), .enable("false")) multiplexer_1 (
    .in0(n29bit_adder_1_out_4), .in1(n29bit_adder_1_out_4), .in2(n29bit_and_1_out_3),
    .in3(n29bit_or_1_out_3), .out(out_4), .sel(Control));
  Negative_Check negative_check_1 (.in_1(out_4), .Output(Flags[3]));
  Zero_Check zero_check_1 (.in_1(out_4), .Output(zero_check_1_output));
  not not_1 (Flags[2], zero_check_1_output);

  // Other names for the same wires on the sheet: Overflow = Flags[0]; Carry = Flags[1]; Zero = Flags[2];
  //   Negative = Flags[3]

  // Notes on the sheet:
  //   29 Bit ALU
  //   0 0 - Adder
  //   0 1 - Subtractor
  //   1 0 - AND
  //   1 1 - OR
  //   Input
  //   A
  //   B
  //   Output
  //   Negative- Zero-Carry-Overflow
  //   Roll - 2207006
endmodule

// AND
module _29bit_AND (
  input  [28:0] in_1,
  input  [28:0] in_2,
  output [28:0] out_3
);

  assign out_3 = in_1 & in_2;  // AND_Gate and_1, 29 bits wide

  // Notes on the sheet:
  //   2207006
  //   A
  //   B
  //   A AND B
endmodule

// OR
module _29bit_OR (
  input  [28:0] in_1,
  input  [28:0] in_2,
  output [28:0] out_3
);

  assign out_3 = in_1 | in_2;  // OR_Gate or_1, 29 bits wide

  // Notes on the sheet:
  //   2207006
  //   A
  //   B
  //   A OR B
endmodule

// Adder
module _29bit_Adder (
  input  in_1,
  input  [28:0] in_2,
  input  [28:0] in_3,
  output [28:0] out_4,
  output out_5,
  output Overflow
);

  wire and_1_out, and_2_out, n1bit_adder_1_cout, n1bit_adder_2_cout, n1bit_adder_3_cout, n1bit_adder_4_cout,
       n1bit_adder_5_cout, n1bit_adder_6_cout, n1bit_adder_7_cout, n1bit_adder_8_cout, n1bit_adder_9_cout,
       n1bit_adder_10_cout, n1bit_adder_11_cout, n1bit_adder_12_cout, n1bit_adder_13_cout,
       n1bit_adder_14_cout, n1bit_adder_15_cout, n1bit_adder_16_cout, n1bit_adder_17_cout,
       n1bit_adder_18_cout, n1bit_adder_19_cout, n1bit_adder_20_cout, n1bit_adder_21_cout,
       n1bit_adder_22_cout, n1bit_adder_23_cout, n1bit_adder_24_cout, n1bit_adder_25_cout,
       n1bit_adder_26_cout, n1bit_adder_27_cout, n1bit_adder_28_cout, not_1_out, not_2_out, not_3_out;
  wire [28:0] bit_extender_1_out, xor_1_out;

  assign bit_extender_1_out = {{28{in_1}}, in_1};  // Bit_Extender bit_extender_1
  assign xor_1_out = bit_extender_1_out ^ in_3;  // XOR_Gate xor_1, 29 bits wide
  _1bit_Adder u_1bit_adder_1 (.Cin(in_1), .A(in_2[0]), .B(xor_1_out[0]), .Sum(out_4[0]), .Cout(n1bit_adder_1_cout));
  _1bit_Adder u_1bit_adder_2 (
    .Cin(n1bit_adder_1_cout), .A(in_2[1]), .B(xor_1_out[1]), .Sum(out_4[1]), .Cout(n1bit_adder_2_cout));
  _1bit_Adder u_1bit_adder_3 (
    .Cin(n1bit_adder_2_cout), .A(in_2[2]), .B(xor_1_out[2]), .Sum(out_4[2]), .Cout(n1bit_adder_3_cout));
  _1bit_Adder u_1bit_adder_4 (
    .Cin(n1bit_adder_3_cout), .A(in_2[3]), .B(xor_1_out[3]), .Sum(out_4[3]), .Cout(n1bit_adder_4_cout));
  _1bit_Adder u_1bit_adder_5 (
    .Cin(n1bit_adder_4_cout), .A(in_2[4]), .B(xor_1_out[4]), .Sum(out_4[4]), .Cout(n1bit_adder_5_cout));
  _1bit_Adder u_1bit_adder_6 (
    .Cin(n1bit_adder_5_cout), .A(in_2[5]), .B(xor_1_out[5]), .Sum(out_4[5]), .Cout(n1bit_adder_6_cout));
  _1bit_Adder u_1bit_adder_7 (
    .Cin(n1bit_adder_6_cout), .A(in_2[6]), .B(xor_1_out[6]), .Sum(out_4[6]), .Cout(n1bit_adder_7_cout));
  _1bit_Adder u_1bit_adder_8 (
    .Cin(n1bit_adder_7_cout), .A(in_2[7]), .B(xor_1_out[7]), .Sum(out_4[7]), .Cout(n1bit_adder_8_cout));
  _1bit_Adder u_1bit_adder_9 (
    .Cin(n1bit_adder_8_cout), .A(in_2[8]), .B(xor_1_out[8]), .Sum(out_4[8]), .Cout(n1bit_adder_9_cout));
  _1bit_Adder u_1bit_adder_10 (
    .Cin(n1bit_adder_9_cout), .A(in_2[9]), .B(xor_1_out[9]), .Sum(out_4[9]), .Cout(n1bit_adder_10_cout));
  _1bit_Adder u_1bit_adder_11 (
    .Cin(n1bit_adder_10_cout), .A(in_2[10]), .B(xor_1_out[10]), .Sum(out_4[10]), .Cout(n1bit_adder_11_cout));
  _1bit_Adder u_1bit_adder_12 (
    .Cin(n1bit_adder_11_cout), .A(in_2[11]), .B(xor_1_out[11]), .Sum(out_4[11]), .Cout(n1bit_adder_12_cout));
  _1bit_Adder u_1bit_adder_13 (
    .Cin(n1bit_adder_12_cout), .A(in_2[12]), .B(xor_1_out[12]), .Sum(out_4[12]), .Cout(n1bit_adder_13_cout));
  _1bit_Adder u_1bit_adder_14 (
    .Cin(n1bit_adder_13_cout), .A(in_2[13]), .B(xor_1_out[13]), .Sum(out_4[13]), .Cout(n1bit_adder_14_cout));
  _1bit_Adder u_1bit_adder_15 (
    .Cin(n1bit_adder_14_cout), .A(in_2[14]), .B(xor_1_out[14]), .Sum(out_4[14]), .Cout(n1bit_adder_15_cout));
  _1bit_Adder u_1bit_adder_16 (
    .Cin(n1bit_adder_15_cout), .A(in_2[15]), .B(xor_1_out[15]), .Sum(out_4[15]), .Cout(n1bit_adder_16_cout));
  _1bit_Adder u_1bit_adder_17 (
    .Cin(n1bit_adder_16_cout), .A(in_2[16]), .B(xor_1_out[16]), .Sum(out_4[16]), .Cout(n1bit_adder_17_cout));
  _1bit_Adder u_1bit_adder_18 (
    .Cin(n1bit_adder_17_cout), .A(in_2[17]), .B(xor_1_out[17]), .Sum(out_4[17]), .Cout(n1bit_adder_18_cout));
  _1bit_Adder u_1bit_adder_19 (
    .Cin(n1bit_adder_18_cout), .A(in_2[18]), .B(xor_1_out[18]), .Sum(out_4[18]), .Cout(n1bit_adder_19_cout));
  _1bit_Adder u_1bit_adder_20 (
    .Cin(n1bit_adder_19_cout), .A(in_2[19]), .B(xor_1_out[19]), .Sum(out_4[19]), .Cout(n1bit_adder_20_cout));
  _1bit_Adder u_1bit_adder_21 (
    .Cin(n1bit_adder_20_cout), .A(in_2[20]), .B(xor_1_out[20]), .Sum(out_4[20]), .Cout(n1bit_adder_21_cout));
  _1bit_Adder u_1bit_adder_22 (
    .Cin(n1bit_adder_21_cout), .A(in_2[21]), .B(xor_1_out[21]), .Sum(out_4[21]), .Cout(n1bit_adder_22_cout));
  _1bit_Adder u_1bit_adder_23 (
    .Cin(n1bit_adder_22_cout), .A(in_2[22]), .B(xor_1_out[22]), .Sum(out_4[22]), .Cout(n1bit_adder_23_cout));
  _1bit_Adder u_1bit_adder_24 (
    .Cin(n1bit_adder_23_cout), .A(in_2[23]), .B(xor_1_out[23]), .Sum(out_4[23]), .Cout(n1bit_adder_24_cout));
  _1bit_Adder u_1bit_adder_25 (
    .Cin(n1bit_adder_24_cout), .A(in_2[24]), .B(xor_1_out[24]), .Sum(out_4[24]), .Cout(n1bit_adder_25_cout));
  _1bit_Adder u_1bit_adder_26 (
    .Cin(n1bit_adder_25_cout), .A(in_2[25]), .B(xor_1_out[25]), .Sum(out_4[25]), .Cout(n1bit_adder_26_cout));
  _1bit_Adder u_1bit_adder_27 (
    .Cin(n1bit_adder_26_cout), .A(in_2[26]), .B(xor_1_out[26]), .Sum(out_4[26]), .Cout(n1bit_adder_27_cout));
  _1bit_Adder u_1bit_adder_28 (
    .Cin(n1bit_adder_27_cout), .A(in_2[27]), .B(xor_1_out[27]), .Sum(out_4[27]), .Cout(n1bit_adder_28_cout));
  _1bit_Adder u_1bit_adder_29 (
    .Cin(n1bit_adder_28_cout), .A(in_2[28]), .B(xor_1_out[28]), .Sum(out_4[28]), .Cout(out_5));
  not not_1 (not_1_out, out_4[28]);
  and and_1 (and_1_out, not_1_out, in_2[28], xor_1_out[28]);
  and and_2 (and_2_out, out_4[28], not_2_out, not_3_out);
  not not_2 (not_2_out, in_2[28]);
  not not_3 (not_3_out, xor_1_out[28]);
  or or_1 (Overflow, and_1_out, and_2_out);

  // Notes on the sheet:
  //   Control ->
  //   A
  //   B
  //   Adder/Subtractor
  //   2207006
  //   SUM
  //   Carry Out
endmodule

// Adder
module _1bit_Adder (
  input  Cin,
  input  A,
  input  B,
  output Sum,
  output Cout
);

  wire and_1_out, and_2_out, xor_1_out;

  xor xor_1 (xor_1_out, A, B);
  and and_1 (and_1_out, B, A);
  xor xor_2 (Sum, Cin, xor_1_out);
  and and_2 (and_2_out, Cin, xor_1_out);
  or or_1 (Cout, and_2_out, and_1_out);

  // Notes on the sheet:
  //   2207006
endmodule

// Zero
module Zero_Check (
  input  [28:0] in_1,
  output Output
);

  or or_1 (Output, in_1[0], in_1[1], in_1[2], in_1[3], in_1[4], in_1[5], in_1[6], in_1[7], in_1[8], in_1[9], in_1[10], in_1[11], in_1[12], in_1[13], in_1[14], in_1[15], in_1[16], in_1[17], in_1[18], in_1[19], in_1[20], in_1[21], in_1[22], in_1[23], in_1[24], in_1[25], in_1[26], in_1[27], in_1[28]);

  // Notes on the sheet:
  //   2207006
  //   Input
endmodule

// Neg
module Negative_Check (
  input  [28:0] in_1,
  output Output
);


  assign Output = in_1[28];

  // Notes on the sheet:
  //   2207006
  //   Input
endmodule
