// Logisim project 4 bit adder.circ as structural Verilog: 2 circuits, main circuit main
module main (
  input  A3,
  input  A2,
  input  A1,
  input  A0,
  input  B3,
  input  B2,
  input  B1,
  input  B0,
  input  C0,
  output C4,
  output S3,
  output S2,
  output S1,
  output S0
);

  wire full_adder_1_cout, full_adder_2_cout, full_adder_3_cout;

  Full_Adder full_adder_1 (.A(B0), .B(A0), .Cin(C0), .S(S0), .Cout(full_adder_1_cout));
  Full_Adder full_adder_2 (.A(B1), .B(A1), .Cin(full_adder_1_cout), .S(S1), .Cout(full_adder_2_cout));
  Full_Adder full_adder_3 (.A(B2), .B(A2), .Cin(full_adder_2_cout), .S(S2), .Cout(full_adder_3_cout));
  Full_Adder full_adder_4 (.A(B3), .B(A3), .Cin(full_adder_3_cout), .S(S3), .Cout(C4));

  // Notes on the sheet:
  //   4 Bit Adder Circuit
  //   C1
  //   C2
  //   C3
  //   2207006
endmodule

module Full_Adder (
  input  A,
  input  B,
  input  Cin,
  output S,
  output Cout
);

  wire and_1_out, and_2_out, and_3_out, and_4_out, and_5_out, and_6_out, and_7_out, not_1_out, not_2_out,
       not_3_out, not_4_out, not_5_out, not_6_out;

  not not_1 (not_1_out, A);
  not not_2 (not_2_out, B);
  not not_3 (not_3_out, A);
  not not_4 (not_4_out, Cin);
  not not_5 (not_5_out, B);
  not not_6 (not_6_out, Cin);
  and and_1 (and_1_out, B, Cin);
  and and_2 (and_2_out, A, Cin);
  and and_3 (and_3_out, A, B);
  and and_4 (and_4_out, not_1_out, not_2_out, Cin);
  and and_5 (and_5_out, not_3_out, B, not_4_out);
  and and_6 (and_6_out, A, not_5_out, not_6_out);
  and and_7 (and_7_out, A, B, Cin);
  or or_1 (Cout, and_1_out, and_2_out, and_3_out);
  or or_2 (S, and_4_out, and_5_out, and_6_out, and_7_out);

  // Notes on the sheet:
  //   Full Adder
endmodule
