// Logisim project CPU_2207006.circ as structural Verilog: 5 circuits, main circuit main
module main (
  input  Reset
);

  wire Clock_out, cpu_1_mem_load, cpu_1_mem_store;
  wire [7:0] cpu_1_out_4;
  wire [28:0] cpu_1_data_out, ram_1_data;

  Clock Clock (.out(Clock_out));
  CPU cpu_1 (
    .Data_In(ram_1_data), .Reset(Reset), .CLK(Clock_out), .out_4(cpu_1_out_4), .Data_Out(cpu_1_data_out),
    .Mem_Store(cpu_1_mem_store), .Mem_Load(cpu_1_mem_load));
  RAM #(.dataWidth(29), .bus("separate")) ram_1 (
    .addr(cpu_1_out_4), .din(cpu_1_data_out), .data(ram_1_data), .str(cpu_1_mem_store), .clk(Clock_out),
    .ld(cpu_1_mem_load));  // open: sel, clr

  // Notes on the sheet:
  //   HLT
  //   Program : 
  //   MVI R1, 0000
  //   MVI  R2, 0001
  //   STR R1, [0020]
  //   STR R2, [0021]
  //   INC R1
  //   STR R1, [0022]
  //   MVI R3, 000A
  //   DEC R3
  //   STR R3, [0023]
  //   ADD R1, R2
  //   STR R1, [0024]
  //   SUB R3, R1
  //   STR R3, [0025]
  //   MVI R4, 0002
  //   MVI R5, 0003
  //   AND R4,R5
  //   STR R4, [0026]
  //   OR R1, R4
  //   DEC R1
  //   STR R6,[0028]
  //   STR R1, [0027]
  //   MVI R6, 000D
  //   Expected Output :
  //   2207006
  //   RAM
  //   Instructions
  //   00 ADD
  //   01 SUB
  //   02 AND
  //   03 OR
  //   04 INC
  //   05 DEC
  //   06 CMP
  //   07 NOP
  //   08 MOV
  //   09 MVI
  //   0A LOD
  //   0B STR
  //   0C JZ
  //   0D JN
  //   0E JMP
  //   0F HLT
endmodule

module CPU (
  input  [28:0] Data_In,
  input  Reset,
  input  CLK,
  output [7:0] out_4,
  output [28:0] Data_Out,
  output Mem_Store,
  output Mem_Load
);

  wire addSel, arithmetic, clock, dataWrite, flagLoad, halt, loadIR, loadMAR, neg, PCload, PCsel, zero;
  wire [1:0] operation, RegInputSel;
  wire [2:0] DesRegSel, SrcRegSel;
  wire [3:0] flags;
  wire [3:2] Flags_q;
  wire [7:0] multiplexer_3_out, pc_increment_1_pc_out, PCout;
  wire [12:0] bit_extender_1_out, IRout;
  wire [15:0] MARout;
  wire [28:0] ALUout, bit_extender_2_out, MBRout, multiplexer_1_out, multiplexer_4_out, srcData;

  assign bit_extender_1_out = {{12{1'b0}}, 1'b0};  // Bit_Extender bit_extender_1
  Register #(.width(16)) MAR (.D(Data_In[15:0]), .en(loadMAR), .Q(MARout), .clk(clock), .clr(Reset));
  Multiplexer #(.width(29), .enable("false")) multiplexer_1 (
    .in0(srcData), .in1(bit_extender_2_out), .out(multiplexer_1_out), .sel(arithmetic));
  assign bit_extender_2_out = {{28{1'b0}}, 1'b1};  // Bit_Extender bit_extender_2
  Multiplexer #(.width(8), .enable("false")) multiplexer_2 (.in0(PCout), .in1(MARout[7:0]), .out(out_4), .sel(addSel));
  Multiplexer #(.width(8), .enable("false")) multiplexer_3 (
    .in0(MARout[7:0]), .in1(pc_increment_1_pc_out), .out(multiplexer_3_out), .sel(PCsel));
  PC_Increment pc_increment_1 (.PC_In(PCout), .PC_Out(pc_increment_1_pc_out));
  Multiplexer #(.select(2), .width(29), .enable("false")) multiplexer_4 (
    .in0({bit_extender_1_out, MARout}), .in1(srcData), .in2(Data_In), .in3(ALUout), .out(multiplexer_4_out),
    .sel(RegInputSel));
  Register #(.width(29)) MBR (.D(Data_In), .en(1'b1), .Q(MBRout), .clk(clock), .clr(Reset));
  _29bit_ALU u_29bit_alu_1 (
    .Control(operation), .in_2(Data_Out), .in_3(multiplexer_1_out), .out_4(ALUout), .Flags(flags));
  Register PC (.D(multiplexer_3_out), .en(PCload), .Q(PCout), .clk(clock), .clr(Reset));
  Register #(.width(4)) u_Flags (.D(flags), .en(flagLoad), .Q({Flags_q, zero, neg}), .clk(clock), .clr(Reset));
  Control_Unit control_unit_1 (
    .Reset(Reset), .IR_value(IRout), .Zero(zero), .Neg(neg), .Clock(clock), .desReg(DesRegSel),
    .srcReg(SrcRegSel), .flag_load(flagLoad), .MAR_load(loadMAR), .PC_Sel(PCsel), .IR_load(loadIR),
    .PC_load(PCload), .operation({arithmetic, operation}), .Halt(halt), .Mem_Write(Mem_Store),
    .Mem_Read(Mem_Load), .Reg_In_Sel(RegInputSel), .Des_Reg_Write(dataWrite), .Address(addSel));
  Register #(.width(13)) IR (.D(Data_In[28:16]), .en(loadIR), .Q(IRout), .clk(clock), .clr(Reset));
  Registers registers_1 (
    .Data_Write(dataWrite), .DesReg(DesRegSel), .Data_In(multiplexer_4_out), .CLK(clock), .Reset(Reset),
    .SrcReg(SrcRegSel), .DesPort(Data_Out), .SrcPort(srcData));
  and and_1 (clock, CLK, ~halt);  // AND_Gate

  // Other names for the same wires on the sheet: address[7:0] = out_4; dataIn[28:0] = Data_In;
  //   desData[28:0] = Data_Out; LoadFromMem = Mem_Load; StoreToMem = Mem_Store

  // Notes on the sheet:
  //   2207006
endmodule

module Registers (
  input  Data_Write,
  input  [2:0] DesReg,
  input  [28:0] Data_In,
  input  CLK,
  input  Reset,
  input  [2:0] SrcReg,
  output [28:0] DesPort,
  output [28:0] SrcPort
);

  wire _0, _1, _2, _3, _4, _5, _6, _7;
  wire [28:0] out0, out1, out2, out3, out4, out5, out6, out7;

  Demultiplexer #(.select(3), .enable("false")) demultiplexer_1 (
    .out0(_0), .out1(_1), .out2(_2), .out3(_3), .out4(_4), .out5(_5), .out6(_6), .out7(_7), .in(Data_Write),
    .sel(DesReg));
  Register #(.width(29)) register_1 (.D(Data_In), .en(_0), .Q(out0), .clk(CLK), .clr(Reset));
  Register #(.width(29)) register_2 (.D(Data_In), .en(_1), .Q(out1), .clk(CLK), .clr(Reset));
  Register #(.width(29)) register_3 (.D(Data_In), .en(_2), .Q(out2), .clk(CLK), .clr(Reset));
  Register #(.width(29)) register_4 (.D(Data_In), .en(_3), .Q(out3), .clk(CLK), .clr(Reset));
  Register #(.width(29)) register_5 (.D(Data_In), .en(_4), .Q(out4), .clk(CLK), .clr(Reset));
  Register #(.width(29)) register_6 (.D(Data_In), .en(_5), .Q(out5), .clk(CLK), .clr(Reset));
  Register #(.width(29)) register_7 (.D(Data_In), .en(_6), .Q(out6), .clk(CLK), .clr(Reset));
  Register #(.width(29)) register_8 (.D(Data_In), .en(_7), .Q(out7), .clk(CLK), .clr(Reset));
  Multiplexer #(.select(3), .width(29), .enable("false")) multiplexer_1 (
    .in0(out0), .in1(out1), .in2(out2), .in3(out3), .in4(out4), .in5(out5), .in6(out6), .in7(out7),
    .out(DesPort), .sel(DesReg));
  Multiplexer #(.select(3), .width(29), .enable("false")) multiplexer_2 (
    .in0(out0), .in1(out1), .in2(out2), .in3(out3), .in4(out4), .in5(out5), .in6(out6), .in7(out7),
    .out(SrcPort), .sel(SrcReg));

  // Other names for the same wires on the sheet: dataIn[28:0] = Data_In; DesRegSel[2:0] = DesReg

  // Notes on the sheet:
  //   2207006
endmodule

module PC_Increment (
  input  [7:0] PC_In,
  output [7:0] PC_Out
);

  wire [7:0] bit_extender_1_out;
  wire [28:8] n29bit_alu_1_out_4;

  assign bit_extender_1_out = {{7{1'b0}}, 1'b1};  // Bit_Extender bit_extender_1
  _29bit_ALU u_29bit_alu_1 (
    .Control(2'b00), .in_2({{21{1'b0}}, PC_In}), .in_3({{21{1'b0}}, bit_extender_1_out}),
    .out_4({n29bit_alu_1_out_4, PC_Out}));  // open: Flags

  // Notes on the sheet:
  //   2207006
endmodule

module Control_Unit (
  input  Reset,
  input  [12:0] IR_value,
  input  Zero,
  input  Neg,
  input  Clock,
  output [2:0] desReg,
  output [2:0] srcReg,
  output flag_load,
  output MAR_load,
  output PC_Sel,
  output IR_load,
  output PC_load,
  output [2:0] operation,
  output Halt,
  output Mem_Write,
  output Mem_Read,
  output [1:0] Reg_In_Sel,
  output Des_Reg_Write,
  output Address
);

  wire and_2_out, and_3_out, and_4_out, and_5_out, and_6_out, and_7_out, multiplexer_3_out,
       multiplexer_11_out, nand_1_out, or_1_out, or_2_out, phase;
  wire [1:0] multiplexer_1_out;

  and and_1 (Halt, IR_value[8], IR_value[9], IR_value[10], IR_value[11]);
  Multiplexer #(.select(4), .width(2), .enable("false")) multiplexer_1 (
    .in0(2'b11), .in1(2'b11), .in2(2'b11), .in3(2'b11), .in4(2'b11), .in5(2'b11), .in6(2'b11), .in7(2'b00),
    .in8(2'b01), .in9(2'b00), .in10(2'b10), .in11(2'b00), .in12(2'b00), .in13(2'b00), .in14(2'b00),
    .in15(2'b00), .out(multiplexer_1_out), .sel(IR_value[11:8]));
  nand nand_1 (nand_1_out, IR_value[8], IR_value[9], IR_value[10]);
  and and_2 (and_2_out, nand_1_out, ~IR_value[11]);  // AND_Gate
  Multiplexer #(.enable("false")) multiplexer_2 (.in0(1'b1), .in1(1'b0), .out(IR_load), .sel(phase));
  Multiplexer #(.enable("false")) multiplexer_3 (.in0(Zero), .in1(Neg), .out(multiplexer_3_out), .sel(IR_value[8]));
  or or_1 (or_1_out, Reset, Halt);
  Multiplexer #(.width(3), .enable("false")) multiplexer_4 (
    .in0(IR_value[10:8]), .in1(3'b001), .out(operation), .sel(and_3_out));
  and and_3 (and_3_out, ~IR_value[8], IR_value[9], IR_value[10]);  // AND_Gate
  Multiplexer #(.enable("false")) multiplexer_5 (.in0(1'b0), .in1(and_4_out), .out(Mem_Write), .sel(phase));
  and and_4 (and_4_out, IR_value[8], IR_value[9], ~IR_value[10], IR_value[11]);  // AND_Gate
  Multiplexer #(.width(2), .enable("false")) multiplexer_6 (
    .in0(2'b00), .in1(multiplexer_1_out), .out(Reg_In_Sel), .sel(phase));
  and and_5 (and_5_out, multiplexer_3_out, ~IR_value[9], IR_value[10], IR_value[11]);  // AND_Gate
  or or_2 (or_2_out, and_5_out, and_6_out);
  and and_6 (and_6_out, ~IR_value[8], IR_value[9], IR_value[10], IR_value[11]);  // AND_Gate
  Counter #(.width(1), .max('h1)) Phase_Counter (
    .Q(phase), .clk(Clock), .clr(or_1_out));  // open: load, D, count, carry
  not not_1 (Mem_Read, Mem_Write);
  and and_7 (and_7_out, IR_value[9], ~IR_value[10], IR_value[11]);  // AND_Gate
  Multiplexer #(.enable("false")) multiplexer_7 (.in0(1'b0), .in1(and_2_out), .out(flag_load), .sel(phase));
  Multiplexer #(.enable("false")) multiplexer_8 (.in0(1'b1), .in1(or_2_out), .out(PC_load), .sel(phase));
  Multiplexer #(.enable("false")) multiplexer_9 (.in0(1'b0), .in1(and_7_out), .out(Address), .sel(phase));
  Multiplexer #(.enable("false")) multiplexer_10 (.in0(1'b1), .in1(1'b0), .out(MAR_load), .sel(phase));
  Multiplexer #(.select(4), .enable("false")) multiplexer_11 (
    .in0(1'b1), .in1(1'b1), .in2(1'b1), .in3(1'b1), .in4(1'b1), .in5(1'b1), .in6(1'b0), .in7(1'b0),
    .in8(1'b1), .in9(1'b1), .in10(1'b1), .in11(1'b0), .in12(1'b0), .in13(1'b0), .in14(1'b0), .in15(1'b0),
    .out(multiplexer_11_out), .sel(IR_value[11:8]));
  Multiplexer #(.enable("false")) multiplexer_12 (.in0(1'b1), .in1(1'b0), .out(PC_Sel), .sel(phase));
  Multiplexer #(.enable("false")) multiplexer_13 (
    .in0(1'b0), .in1(multiplexer_11_out), .out(Des_Reg_Write), .sel(phase));

  assign desReg = IR_value[6:4];
  assign srcReg = IR_value[2:0];

  // Other names for the same wires on the sheet: opcode[3:0] = IR_value[11:8]; operation_t[2:0] = IR_value[10:8]

  // Notes on the sheet:
  //   2207006
  //   Load IR
  //   Phase Selector
  //   Operation for ALU
  //   Halt
  //   Read-Write Logic
  //   Instructions
  //   Enable Flag
  //   Load PC
  //   Address Load
  //   RESET
  //   Load MAR
  //   Select PC
endmodule
