// Logisim project Multiplier_2207006.circ as structural Verilog: 17 circuits, main circuit Booth's Multiplier
module Booth_s_Multiplier (
  input  [28:0] in_1,
  input  [28:0] in_2,
  input  Reset,
  output [28:0] out_4,
  output [28:0] out_5
);

  wire clock_1_out, controller_1_c1, controller_1_clear__a__q_1, controller_1_dec_cnt,
       controller_1_load__m__q__cnt, controller_1_load_a, controller_1_shift, or_1_out, shift_register_1_out,
       shift_register_3_out, shift_register_4_q0;
  wire [1:0] controller_1_c0;
  wire [4:0] counter_1_q;
  wire [28:0] n2_s_compliment_1_out_2, n2_s_compliment_2_out_2, n29bit_alu_1_out_4, shift_register_2_q28;

  _2_s_Compliment u_2_s_compliment_1 (.in_1(in_1), .out_2(n2_s_compliment_1_out_2));
  _2_s_Compliment u_2_s_compliment_2 (.in_1(in_2), .out_2(n2_s_compliment_2_out_2));
  Clock clock_1 (.out(clock_1_out));
  controller controller_1 (
    .Clk(clock_1_out), .Reset(Reset), .Q0(out_5[0]), .Q_1(shift_register_4_q0), .Count(counter_1_q),
    .Clear__A__Q_1(controller_1_clear__a__q_1), .Load__M__Q__Cnt(controller_1_load__m__q__cnt),
    .Load_A(controller_1_load_a), .C0(controller_1_c0[0]), .C1(controller_1_c1), .Shift(controller_1_shift),
    .Dec_Cnt(controller_1_dec_cnt));
  or or_1 (or_1_out, controller_1_dec_cnt, controller_1_load__m__q__cnt);
  Counter #(.width(5), .max('h1d)) counter_1 (
    .load(or_1_out), .D(5'b11101), .count(controller_1_dec_cnt), .Q(counter_1_q), .clk(clock_1_out));  // open: carry, clr
  Shift_Register #(.length(29)) shift_register_1 (
    .shift(controller_1_shift), .in(out_4[28]), .clk(clock_1_out), .out(shift_register_1_out),
    .load(controller_1_load_a), .clr(controller_1_clear__a__q_1), .d0(n29bit_alu_1_out_4[28]),
    .q0(out_4[28]), .d1(n29bit_alu_1_out_4[27]), .q1(out_4[27]), .d2(n29bit_alu_1_out_4[26]), .q2(out_4[26]),
    .d3(n29bit_alu_1_out_4[25]), .q3(out_4[25]), .d4(n29bit_alu_1_out_4[24]), .q4(out_4[24]),
    .d5(n29bit_alu_1_out_4[23]), .q5(out_4[23]), .d6(n29bit_alu_1_out_4[22]), .q6(out_4[22]),
    .d7(n29bit_alu_1_out_4[21]), .q7(out_4[21]), .d8(n29bit_alu_1_out_4[20]), .q8(out_4[20]),
    .d9(n29bit_alu_1_out_4[19]), .q9(out_4[19]), .d10(n29bit_alu_1_out_4[18]), .q10(out_4[18]),
    .d11(n29bit_alu_1_out_4[17]), .q11(out_4[17]), .d12(n29bit_alu_1_out_4[16]), .q12(out_4[16]),
    .d13(n29bit_alu_1_out_4[15]), .q13(out_4[15]), .d14(n29bit_alu_1_out_4[14]), .q14(out_4[14]),
    .d15(n29bit_alu_1_out_4[13]), .q15(out_4[13]), .d16(n29bit_alu_1_out_4[12]), .q16(out_4[12]),
    .d17(n29bit_alu_1_out_4[11]), .q17(out_4[11]), .d18(n29bit_alu_1_out_4[10]), .q18(out_4[10]),
    .d19(n29bit_alu_1_out_4[9]), .q19(out_4[9]), .d20(n29bit_alu_1_out_4[8]), .q20(out_4[8]),
    .d21(n29bit_alu_1_out_4[7]), .q21(out_4[7]), .d22(n29bit_alu_1_out_4[6]), .q22(out_4[6]),
    .d23(n29bit_alu_1_out_4[5]), .q23(out_4[5]), .d24(n29bit_alu_1_out_4[4]), .q24(out_4[4]),
    .d25(n29bit_alu_1_out_4[3]), .q25(out_4[3]), .d26(n29bit_alu_1_out_4[2]), .q26(out_4[2]),
    .d27(n29bit_alu_1_out_4[1]), .q27(out_4[1]), .d28(n29bit_alu_1_out_4[0]), .q28(out_4[0]));
  not not_1 (controller_1_c0[1], controller_1_c1);
  Shift_Register #(.length(29)) shift_register_2 (
    .shift(1'b0), .clk(clock_1_out), .load(controller_1_load__m__q__cnt), .d0(n2_s_compliment_1_out_2[28]),
    .q0(shift_register_2_q28[28]), .d1(n2_s_compliment_1_out_2[27]), .q1(shift_register_2_q28[27]),
    .d2(n2_s_compliment_1_out_2[26]), .q2(shift_register_2_q28[26]), .d3(n2_s_compliment_1_out_2[25]),
    .q3(shift_register_2_q28[25]), .d4(n2_s_compliment_1_out_2[24]), .q4(shift_register_2_q28[24]),
    .d5(n2_s_compliment_1_out_2[23]), .q5(shift_register_2_q28[23]), .d6(n2_s_compliment_1_out_2[22]),
    .q6(shift_register_2_q28[22]), .d7(n2_s_compliment_1_out_2[21]), .q7(shift_register_2_q28[21]),
    .d8(n2_s_compliment_1_out_2[20]), .q8(shift_register_2_q28[20]), .d9(n2_s_compliment_1_out_2[19]),
    .q9(shift_register_2_q28[19]), .d10(n2_s_compliment_1_out_2[18]), .q10(shift_register_2_q28[18]),
    .d11(n2_s_compliment_1_out_2[17]), .q11(shift_register_2_q28[17]), .d12(n2_s_compliment_1_out_2[16]),
    .q12(shift_register_2_q28[16]), .d13(n2_s_compliment_1_out_2[15]), .q13(shift_register_2_q28[15]),
    .d14(n2_s_compliment_1_out_2[14]), .q14(shift_register_2_q28[14]), .d15(n2_s_compliment_1_out_2[13]),
    .q15(shift_register_2_q28[13]), .d16(n2_s_compliment_1_out_2[12]), .q16(shift_register_2_q28[12]),
    .d17(n2_s_compliment_1_out_2[11]), .q17(shift_register_2_q28[11]), .d18(n2_s_compliment_1_out_2[10]),
    .q18(shift_register_2_q28[10]), .d19(n2_s_compliment_1_out_2[9]), .q19(shift_register_2_q28[9]),
    .d20(n2_s_compliment_1_out_2[8]), .q20(shift_register_2_q28[8]), .d21(n2_s_compliment_1_out_2[7]),
    .q21(shift_register_2_q28[7]), .d22(n2_s_compliment_1_out_2[6]), .q22(shift_register_2_q28[6]),
    .d23(n2_s_compliment_1_out_2[5]), .q23(shift_register_2_q28[5]), .d24(n2_s_compliment_1_out_2[4]),
    .q24(shift_register_2_q28[4]), .d25(n2_s_compliment_1_out_2[3]), .q25(shift_register_2_q28[3]),
    .d26(n2_s_compliment_1_out_2[2]), .q26(shift_register_2_q28[2]), .d27(n2_s_compliment_1_out_2[1]),
    .q27(shift_register_2_q28[1]), .d28(n2_s_compliment_1_out_2[0]), .q28(shift_register_2_q28[0]));  // open: in, out, clr
  _29bit_ALU u_29bit_alu_1 (
    .Control(controller_1_c0), .in_2(out_4), .in_3(shift_register_2_q28), .out_4(n29bit_alu_1_out_4));  // open: Flags
  Shift_Register #(.length(29)) shift_register_3 (
    .shift(controller_1_shift), .in(shift_register_1_out), .clk(clock_1_out), .out(shift_register_3_out),
    .load(controller_1_load__m__q__cnt), .d0(n2_s_compliment_2_out_2[28]), .q0(out_5[28]),
    .d1(n2_s_compliment_2_out_2[27]), .q1(out_5[27]), .d2(n2_s_compliment_2_out_2[26]), .q2(out_5[26]),
    .d3(n2_s_compliment_2_out_2[25]), .q3(out_5[25]), .d4(n2_s_compliment_2_out_2[24]), .q4(out_5[24]),
    .d5(n2_s_compliment_2_out_2[23]), .q5(out_5[23]), .d6(n2_s_compliment_2_out_2[22]), .q6(out_5[22]),
    .d7(n2_s_compliment_2_out_2[21]), .q7(out_5[21]), .d8(n2_s_compliment_2_out_2[20]), .q8(out_5[20]),
    .d9(n2_s_compliment_2_out_2[19]), .q9(out_5[19]), .d10(n2_s_compliment_2_out_2[18]), .q10(out_5[18]),
    .d11(n2_s_compliment_2_out_2[17]), .q11(out_5[17]), .d12(n2_s_compliment_2_out_2[16]), .q12(out_5[16]),
    .d13(n2_s_compliment_2_out_2[15]), .q13(out_5[15]), .d14(n2_s_compliment_2_out_2[14]), .q14(out_5[14]),
    .d15(n2_s_compliment_2_out_2[13]), .q15(out_5[13]), .d16(n2_s_compliment_2_out_2[12]), .q16(out_5[12]),
    .d17(n2_s_compliment_2_out_2[11]), .q17(out_5[11]), .d18(n2_s_compliment_2_out_2[10]), .q18(out_5[10]),
    .d19(n2_s_compliment_2_out_2[9]), .q19(out_5[9]), .d20(n2_s_compliment_2_out_2[8]), .q20(out_5[8]),
    .d21(n2_s_compliment_2_out_2[7]), .q21(out_5[7]), .d22(n2_s_compliment_2_out_2[6]), .q22(out_5[6]),
    .d23(n2_s_compliment_2_out_2[5]), .q23(out_5[5]), .d24(n2_s_compliment_2_out_2[4]), .q24(out_5[4]),
    .d25(n2_s_compliment_2_out_2[3]), .q25(out_5[3]), .d26(n2_s_compliment_2_out_2[2]), .q26(out_5[2]),
    .d27(n2_s_compliment_2_out_2[1]), .q27(out_5[1]), .d28(n2_s_compliment_2_out_2[0]), .q28(out_5[0]));  // open: clr
  Shift_Register #(.length(1)) shift_register_4 (
    .shift(controller_1_shift), .in(shift_register_3_out), .clk(clock_1_out),
    .clr(controller_1_clear__a__q_1), .q0(shift_register_4_q0));  // open: out, load, d0

  // Notes on the sheet:
  //   Multiplicand
  //   Multiplier
  //   29 Bit Multiplier
  //   M
  //   Q
  //   Result
  //   Clock
  //   A
  //   ALU
  //   Q
  //   Roll - 2207006
  //   Q-1
endmodule

module _29bit_ALU (
  input  [1:0] Control,
  input  [28:0] in_2,
  input  [28:0] in_3,
  output [28:0] out_4,
  output [3:0] Flags
);

  wire zero_check_1_output;
  wire [28:0] n29_bit_parallel_adder_1_out_4, n29bit_and_1_out_3, n29bit_or_1_out_3;

  _29bit_AND u_29bit_and_1 (.in_1(in_2), .in_2(in_3), .out_3(n29bit_and_1_out_3));
  _29bit_OR u_29bit_or_1 (.in_1(in_3), .in_2(in_2), .out_3(n29bit_or_1_out_3));
  _29_bit_Parallel_Adder u_29_bit_parallel_adder_1 (
    .in_1(Control[0]), .in_2(in_2), .in_3(in_3), .out_4(n29_bit_parallel_adder_1_out_4), .out_5(Flags[1]),
    .out_6(Flags[0]));
  _4x1_mux u_4x1_mux_1 (
    .in_1(Control), .in_2(n29_bit_parallel_adder_1_out_4), .in_3(n29_bit_parallel_adder_1_out_4),
    .in_4(n29bit_and_1_out_3), .in_5(n29bit_or_1_out_3), .out_6(out_4));
  Negative_Check negative_check_1 (.in_1(out_4), .Output(Flags[3]));
  Zero_Check zero_check_1 (.in_1(out_4), .Output(zero_check_1_output));
  not not_1 (Flags[2], zero_check_1_output);

  // Other names for the same wires on the sheet: Overflow = Flags[0]; Carry = Flags[1]; Zero = Flags[2];
  //   Negative = Flags[3]

  // Notes on the sheet:
  //   29 Bit ALU
  //   0 0 - Adder
  //   0 1 - Subtractor
  //   1 0 - AND
  //   1 1 - OR
  //   Input
  //   A
  //   B
  //   Output
  //   Negative- Zero-Carry-Overflow
  //   Roll - 2207006
endmodule

// AND
module _29bit_AND (
  input  [28:0] in_1,
  input  [28:0] in_2,
  output [28:0] out_3
);

  assign out_3 = in_1 & in_2;  // AND_Gate and_1, 29 bits wide

  // Notes on the sheet:
  //   2207006
  //   A
  //   B
  //   A AND B
endmodule

// OR
module _29bit_OR (
  input  [28:0] in_1,
  input  [28:0] in_2,
  output [28:0] out_3
);

  assign out_3 = in_1 | in_2;  // OR_Gate or_1, 29 bits wide

  // Notes on the sheet:
  //   2207006
  //   A
  //   B
  //   A OR B
endmodule

// Adder
module _1bit_Adder (
  input  Cin,
  input  A,
  input  B,
  output Sum,
  output Cout
);

  wire and_1_out, and_2_out, xor_1_out;

  xor xor_1 (xor_1_out, A, B);
  and and_1 (and_1_out, B, A);
  xor xor_2 (Sum, Cin, xor_1_out);
  and and_2 (and_2_out, Cin, xor_1_out);
  or or_1 (Cout, and_2_out, and_1_out);

  // Notes on the sheet:
  //   2207006
endmodule

// Zero
module Zero_Check (
  input  [28:0] in_1,
  output Output
);

  or or_1 (Output, in_1[0], in_1[1], in_1[2], in_1[3], in_1[4], in_1[5], in_1[6], in_1[7], in_1[8], in_1[9], in_1[10], in_1[11], in_1[12], in_1[13], in_1[14], in_1[15], in_1[16], in_1[17], in_1[18], in_1[19], in_1[20], in_1[21], in_1[22], in_1[23], in_1[24], in_1[25], in_1[26], in_1[27], in_1[28]);

  // Notes on the sheet:
  //   2207006
  //   Input
endmodule

// Neg
module Negative_Check (
  input  [28:0] in_1,
  output Output
);


  assign Output = in_1[28];

  // Notes on the sheet:
  //   2207006
  //   Input
endmodule

module _29bit_CLG (
  input  Cin,
  input  [28:0] in_2,
  input  [28:0] in_3,
  output [28:0] out_4
);

  _4bit_CLG u_4bit_clg_1 (
    .Cin(Cin), .in_2(in_2[3:0]), .in_3(in_3[3:0]), .C1(out_4[0]), .C2(out_4[1]), .C3(out_4[2]), .C4(out_4[3]));
  _4bit_CLG u_4bit_clg_2 (
    .Cin(out_4[3]), .in_2(in_2[7:4]), .in_3(in_3[7:4]), .C1(out_4[4]), .C2(out_4[5]), .C3(out_4[6]),
    .C4(out_4[7]));
  _4bit_CLG u_4bit_clg_3 (
    .Cin(out_4[7]), .in_2(in_2[11:8]), .in_3(in_3[11:8]), .C1(out_4[8]), .C2(out_4[9]), .C3(out_4[10]),
    .C4(out_4[11]));
  _4bit_CLG u_4bit_clg_4 (
    .Cin(out_4[11]), .in_2(in_2[15:12]), .in_3(in_3[15:12]), .C1(out_4[12]), .C2(out_4[13]), .C3(out_4[14]),
    .C4(out_4[15]));
  _4bit_CLG u_4bit_clg_5 (
    .Cin(out_4[15]), .in_2(in_2[19:16]), .in_3(in_3[19:16]), .C1(out_4[16]), .C2(out_4[17]), .C3(out_4[18]),
    .C4(out_4[19]));
  _4bit_CLG u_4bit_clg_6 (
    .Cin(out_4[19]), .in_2(in_2[23:20]), .in_3(in_3[23:20]), .C1(out_4[20]), .C2(out_4[21]), .C3(out_4[22]),
    .C4(out_4[23]));
  _4bit_CLG u_4bit_clg_7 (
    .Cin(out_4[23]), .in_2(in_2[27:24]), .in_3(in_3[27:24]), .C1(out_4[24]), .C2(out_4[25]), .C3(out_4[26]),
    .C4(out_4[27]));
  _1bit_carry u_1bit_carry_1 (.Cin(out_4[27]), .A(in_2[28]), .B(in_3[28]), .Cout(out_4[28]));

  // Notes on the sheet:
  //   A
  //   B
  //   Cout
  //   2207006
endmodule

module _4bit_CLG (
  input  Cin,
  input  [3:0] in_2,
  input  [3:0] in_3,
  output C1,
  output C2,
  output C3,
  output C4
);

  wire and_1_out, and_2_out, and_3_out, and_4_out, and_5_out, and_6_out, and_7_out, and_8_out, and_9_out,
       and_10_out, and_11_out, and_12_out, and_13_out, and_14_out, xor_1_out, xor_2_out, xor_3_out, xor_4_out;

  xor xor_1 (xor_1_out, in_2[0], in_3[0]);
  xor xor_2 (xor_2_out, in_2[1], in_3[1]);
  xor xor_3 (xor_3_out, in_2[2], in_3[2]);
  xor xor_4 (xor_4_out, in_2[3], in_3[3]);
  and and_1 (and_1_out, in_2[0], in_3[0]);
  and and_2 (and_2_out, in_2[1], in_3[1]);
  and and_3 (and_3_out, in_2[2], in_3[2]);
  and and_4 (and_4_out, in_2[3], in_3[3]);
  and and_5 (and_5_out, Cin, xor_1_out);
  and and_6 (and_6_out, Cin, xor_1_out, xor_2_out);
  and and_7 (and_7_out, xor_2_out, and_1_out);
  and and_8 (and_8_out, xor_3_out, xor_2_out, xor_1_out, Cin);
  and and_9 (and_9_out, and_1_out, xor_2_out, xor_3_out);
  and and_10 (and_10_out, xor_3_out, and_2_out);
  and and_11 (and_11_out, xor_4_out, and_3_out);
  and and_12 (and_12_out, xor_4_out, xor_3_out, and_2_out);
  and and_13 (and_13_out, xor_4_out, xor_3_out, xor_2_out, and_1_out);
  and and_14 (and_14_out, xor_4_out, xor_3_out, xor_2_out, xor_1_out, Cin);
  or or_1 (C1, and_5_out, and_1_out);
  or or_2 (C2, and_6_out, and_7_out, and_2_out);
  or or_3 (C3, and_8_out, and_9_out, and_10_out, and_3_out);
  or or_4 (C4, and_14_out, and_13_out, and_12_out, and_11_out, and_4_out);

  // Notes on the sheet:
  //   A
  //   B
  //   2207006
endmodule

// 1bit CLG
module _1bit_carry (
  input  Cin,
  input  A,
  input  B,
  output Cout
);

  wire and_1_out, and_2_out, xor_1_out;

  and and_1 (and_1_out, A, B);
  xor xor_1 (xor_1_out, A, B);
  and and_2 (and_2_out, xor_1_out, Cin);
  or or_1 (Cout, and_1_out, and_2_out);

  // Notes on the sheet:
  //   2207006
endmodule

module _4_bit_Parallel_Adder (
  input  [3:0] in_1,
  input  [3:0] in_2,
  input  [3:0] in_3,
  output [3:0] out_4
);

  _1bit_Adder u_1bit_adder_1 (.Cin(in_1[0]), .A(in_2[0]), .B(in_3[0]), .Sum(out_4[0]));  // open: Cout
  _1bit_Adder u_1bit_adder_2 (.Cin(in_1[1]), .A(in_2[1]), .B(in_3[1]), .Sum(out_4[1]));  // open: Cout
  _1bit_Adder u_1bit_adder_3 (.Cin(in_1[2]), .A(in_2[2]), .B(in_3[2]), .Sum(out_4[2]));  // open: Cout
  _1bit_Adder u_1bit_adder_4 (.Cin(in_1[3]), .A(in_2[3]), .B(in_3[3]), .Sum(out_4[3]));  // open: Cout

  // Notes on the sheet:
  //   2207006
endmodule

// Add-Sub
module _29_bit_Parallel_Adder (
  input  in_1,
  input  [28:0] in_2,
  input  [28:0] in_3,
  output [28:0] out_4,
  output out_5,
  output out_6
);

  wire and_1_out, and_2_out, not_1_out, not_2_out, not_3_out;
  wire [3:0] xor_1_out_2, xor_1_out_3;
  wire [27:0] n29bit_clg_1_out_4;
  wire [28:0] bit_extender_1_out, xor_1_out;

  assign bit_extender_1_out = {{28{in_1}}, in_1};  // Bit_Extender bit_extender_1
  _29bit_CLG u_29bit_clg_1 (
    .Cin(in_1), .in_2(in_2),
    .in_3({xor_1_out[28], xor_1_out_3, xor_1_out[23:20], xor_1_out_2, xor_1_out[15:0]}),
    .out_4({out_5, n29bit_clg_1_out_4}));
  assign {xor_1_out[28], xor_1_out_3, xor_1_out[23:20], xor_1_out_2, xor_1_out[15:0]} = in_3 ^ bit_extender_1_out;  // XOR_Gate xor_1, 29 bits wide
  _4_bit_Parallel_Adder u_4_bit_parallel_adder_1 (
    .in_1({n29bit_clg_1_out_4[2:0], in_1}), .in_2(in_2[3:0]), .in_3(xor_1_out[3:0]), .out_4(out_4[3:0]));
  _4_bit_Parallel_Adder u_4_bit_parallel_adder_2 (
    .in_1(n29bit_clg_1_out_4[6:3]), .in_2(in_2[7:4]), .in_3(xor_1_out[7:4]), .out_4(out_4[7:4]));
  _4_bit_Parallel_Adder u_4_bit_parallel_adder_3 (
    .in_1(n29bit_clg_1_out_4[10:7]), .in_2(in_2[11:8]), .in_3(xor_1_out[11:8]), .out_4(out_4[11:8]));
  _4_bit_Parallel_Adder u_4_bit_parallel_adder_4 (
    .in_1(n29bit_clg_1_out_4[14:11]), .in_2(in_2[15:12]), .in_3(xor_1_out[15:12]), .out_4(out_4[15:12]));
  _4_bit_Parallel_Adder u_4_bit_parallel_adder_5 (
    .in_1(n29bit_clg_1_out_4[18:15]), .in_2(in_2[19:16]), .in_3(xor_1_out_2), .out_4(out_4[19:16]));
  _4_bit_Parallel_Adder u_4_bit_parallel_adder_6 (
    .in_1(n29bit_clg_1_out_4[22:19]), .in_2(in_2[23:20]), .in_3(xor_1_out[23:20]), .out_4(out_4[23:20]));
  _4_bit_Parallel_Adder u_4_bit_parallel_adder_7 (
    .in_1(n29bit_clg_1_out_4[26:23]), .in_2(in_2[27:24]), .in_3(xor_1_out_3), .out_4(out_4[27:24]));
  _1bit_Adder u_1bit_adder_1 (
    .Cin(n29bit_clg_1_out_4[27]), .A(in_2[28]), .B(xor_1_out[28]), .Sum(out_4[28]));  // open: Cout
  not not_1 (not_1_out, in_2[28]);
  not not_2 (not_2_out, xor_1_out[28]);
  and and_1 (and_1_out, not_1_out, not_2_out, out_4[28]);
  not not_3 (not_3_out, out_4[28]);
  and and_2 (and_2_out, not_3_out, in_2[28], xor_1_out[28]);
  or or_1 (out_6, and_1_out, and_2_out);

  // Notes on the sheet:
  //   2207006
  //   A
  //   B
endmodule

// 4x1
module _4x1_mux (
  input  [1:0] in_1,
  input  [28:0] in_2,
  input  [28:0] in_3,
  input  [28:0] in_4,
  input  [28:0] in_5,
  output [28:0] out_6
);

  wire [28:0] and_1_out, and_2_out, and_3_out, and_4_out, bit_extender_1_out, bit_extender_2_out, not_1_out,
       not_2_out, not_3_out, not_4_out;

  assign bit_extender_1_out = {{28{in_1[0]}}, in_1[0]};  // Bit_Extender bit_extender_1
  assign bit_extender_2_out = {{28{in_1[1]}}, in_1[1]};  // Bit_Extender bit_extender_2
  assign not_1_out = ~bit_extender_1_out;  // NOT_Gate not_1, 29 bits wide
  assign not_2_out = ~bit_extender_2_out;  // NOT_Gate not_2, 29 bits wide
  assign not_3_out = ~bit_extender_2_out;  // NOT_Gate not_3, 29 bits wide
  assign not_4_out = ~bit_extender_1_out;  // NOT_Gate not_4, 29 bits wide
  assign and_1_out = not_1_out & not_2_out & in_2;  // AND_Gate and_1, 29 bits wide
  assign and_2_out = bit_extender_1_out & not_3_out & in_3;  // AND_Gate and_2, 29 bits wide
  assign and_3_out = not_4_out & bit_extender_2_out & in_4;  // AND_Gate and_3, 29 bits wide
  assign and_4_out = bit_extender_1_out & bit_extender_2_out & in_5;  // AND_Gate and_4, 29 bits wide
  assign out_6 = and_1_out | and_2_out | and_3_out | and_4_out;  // OR_Gate or_1, 29 bits wide

  // Notes on the sheet:
  //   2207006
endmodule

module controller (
  input  Clk,
  input  Reset,
  input  Q0,
  input  Q_1,
  input  [4:0] Count,
  output Clear__A__Q_1,
  output Load__M__Q__Cnt,
  output Load_A,
  output C0,
  output C1,
  output Shift,
  output Dec_Cnt
);

  wire counter_1_da, counter_1_db, counter_1_dc, nor_1_out, T0, T2, T4, T6, T7;
  wire [2:0] T;

  Decoder #(.select(3), .enable("false")) decoder_1 (
    .out0(T0), .out1(Clear__A__Q_1), .out2(T2), .out3(C0), .out4(T4), .out5(Dec_Cnt), .out6(T6), .out7(T7),
    .sel(T));
  counter counter_1 (.Q({Q0, Q_1}), .T(T), .C(nor_1_out), .DA(counter_1_da), .DB(counter_1_db), .DC(counter_1_dc));
  nor nor_1 (nor_1_out, Count[2], Count[3], Count[0], Count[1], Count[4]);
  D_Flip_Flop d_ff_1 (.clk(Clk), .D(counter_1_da), .Q(T[0]), .reset(Reset));  // open: Qn, preset, en
  D_Flip_Flop d_ff_2 (.clk(Clk), .D(counter_1_db), .Q(T[1]), .reset(Reset));  // open: Qn, preset, en
  D_Flip_Flop d_ff_3 (.clk(Clk), .D(counter_1_dc), .Q(T[2]), .reset(Reset));  // open: Qn, preset, en
  or or_1 (Load_A, C0, T4);
  or or_2 (C1, T4, C0);

  assign Load__M__Q__Cnt = Clear__A__Q_1;
  assign Shift = Dec_Cnt;

  // Other names for the same wires on the sheet: T1 = Clear__A__Q_1; T3 = C0; T5 = Dec_Cnt

  // Notes on the sheet:
  //   Controller
endmodule

module counter (
  input  [1:0] Q,
  input  [2:0] T,
  input  C,
  output DA,
  output DB,
  output DC
);

  wire and_1_out, and_2_out, and_3_out, and_4_out, and_5_out, or_4_out, or_5_out, Q0, Q1, Q2, Q3, T0, T1, T2,
       T3, T4, T5, T6, T7;

  Decoder #(.select(2), .enable("false")) decoder_1 (.out0(Q0), .out1(Q1), .out2(Q2), .out3(Q3), .sel(Q));
  Decoder #(.select(3), .enable("false")) decoder_2 (
    .out0(T0), .out1(T1), .out2(T2), .out3(T3), .out4(T4), .out5(T5), .out6(T6), .out7(T7), .sel(T));
  or or_1 (DA, T0, and_2_out, T3, T4, and_3_out, T7);
  or or_2 (DB, T1, and_4_out, T5, T6, T6, T7);
  or or_3 (DC, T5, and_5_out, T3, T4, and_1_out, T7);
  and and_1 (and_1_out, T6, C);
  and and_2 (and_2_out, T2, or_4_out);
  and and_3 (and_3_out, T6, C);
  and and_4 (and_4_out, T2, Q2);
  and and_5 (and_5_out, T2, or_5_out);
  or or_4 (or_4_out, Q0, Q2, Q3);
  or or_5 (or_5_out, Q0, Q1, Q3);

  // Notes on the sheet:
  //   Counter
endmodule

module _2_s_Compliment (
  input  [28:0] in_1,
  output [28:0] out_2
);

  wire [27:0] not_1_out;
  wire [28:0] n29bit_alu_1_out_4;

  not not_1 (not_1_out[0], in_1[0]);
  not not_2 (not_1_out[1], in_1[1]);
  not not_3 (not_1_out[2], in_1[2]);
  not not_4 (not_1_out[3], in_1[3]);
  not not_5 (not_1_out[4], in_1[4]);
  not not_6 (not_1_out[5], in_1[5]);
  not not_7 (not_1_out[6], in_1[6]);
  not not_8 (not_1_out[7], in_1[7]);
  not not_9 (not_1_out[8], in_1[8]);
  not not_10 (not_1_out[9], in_1[9]);
  not not_11 (not_1_out[10], in_1[10]);
  not not_12 (not_1_out[11], in_1[11]);
  not not_13 (not_1_out[12], in_1[12]);
  not not_14 (not_1_out[13], in_1[13]);
  not not_15 (not_1_out[14], in_1[14]);
  not not_16 (not_1_out[15], in_1[15]);
  not not_17 (not_1_out[16], in_1[16]);
  not not_18 (not_1_out[17], in_1[17]);
  not not_19 (not_1_out[18], in_1[18]);
  not not_20 (not_1_out[19], in_1[19]);
  not not_21 (not_1_out[20], in_1[20]);
  not not_22 (not_1_out[21], in_1[21]);
  not not_23 (not_1_out[22], in_1[22]);
  not not_24 (not_1_out[23], in_1[23]);
  not not_25 (not_1_out[24], in_1[24]);
  not not_26 (not_1_out[25], in_1[25]);
  not not_27 (not_1_out[26], in_1[26]);
  not not_28 (not_1_out[27], in_1[27]);
  Multiplexer #(.width(29), .enable("false")) multiplexer_1 (
    .in0(in_1), .in1(n29bit_alu_1_out_4), .out(out_2), .sel(in_1[28]));
  _29bit_ALU u_29bit_alu_1 (
    .Control(2'b00), .in_2({in_1[28], not_1_out}), .in_3(29'h1), .out_4(n29bit_alu_1_out_4));  // open: Flags

  // Notes on the sheet:
  //   2's Complement
endmodule

module _58_bit_2_s_Comp (
  input  [28:0] in_1,
  input  [28:0] in_2,
  output [28:0] out_3,
  output [28:0] out_4
);

  wire xor_1_out;
  wire [27:0] not_1_out;
  wire [28:0] multiplexer_1_out, n29bit_alu_1_out_4, n29bit_alu_2_out_4, not_29_out;

  not not_1 (not_1_out[0], in_1[0]);
  not not_2 (not_1_out[1], in_1[1]);
  not not_3 (not_1_out[2], in_1[2]);
  not not_4 (not_1_out[3], in_1[3]);
  not not_5 (not_1_out[4], in_1[4]);
  not not_6 (not_1_out[5], in_1[5]);
  not not_7 (not_1_out[6], in_1[6]);
  not not_8 (not_1_out[7], in_1[7]);
  not not_9 (not_1_out[8], in_1[8]);
  not not_10 (not_1_out[9], in_1[9]);
  not not_11 (not_1_out[10], in_1[10]);
  not not_12 (not_1_out[11], in_1[11]);
  not not_13 (not_1_out[12], in_1[12]);
  not not_14 (not_1_out[13], in_1[13]);
  not not_15 (not_1_out[14], in_1[14]);
  not not_16 (not_1_out[15], in_1[15]);
  not not_17 (not_1_out[16], in_1[16]);
  not not_18 (not_1_out[17], in_1[17]);
  not not_19 (not_1_out[18], in_1[18]);
  not not_20 (not_1_out[19], in_1[19]);
  not not_21 (not_1_out[20], in_1[20]);
  not not_22 (not_1_out[21], in_1[21]);
  not not_23 (not_1_out[22], in_1[22]);
  not not_24 (not_1_out[23], in_1[23]);
  not not_25 (not_1_out[24], in_1[24]);
  not not_26 (not_1_out[25], in_1[25]);
  not not_27 (not_1_out[26], in_1[26]);
  not not_28 (not_1_out[27], in_1[27]);
  not not_29 (not_29_out[0], in_2[0]);
  not not_30 (not_29_out[1], in_2[1]);
  not not_31 (not_29_out[2], in_2[2]);
  not not_32 (not_29_out[3], in_2[3]);
  not not_33 (not_29_out[4], in_2[4]);
  not not_34 (not_29_out[5], in_2[5]);
  not not_35 (not_29_out[6], in_2[6]);
  not not_36 (not_29_out[7], in_2[7]);
  not not_37 (not_29_out[8], in_2[8]);
  not not_38 (not_29_out[9], in_2[9]);
  not not_39 (not_29_out[10], in_2[10]);
  not not_40 (not_29_out[11], in_2[11]);
  not not_41 (not_29_out[12], in_2[12]);
  not not_42 (not_29_out[13], in_2[13]);
  not not_43 (not_29_out[14], in_2[14]);
  not not_44 (not_29_out[15], in_2[15]);
  not not_45 (not_29_out[16], in_2[16]);
  not not_46 (not_29_out[17], in_2[17]);
  not not_47 (not_29_out[18], in_2[18]);
  not not_48 (not_29_out[19], in_2[19]);
  not not_49 (not_29_out[20], in_2[20]);
  not not_50 (not_29_out[21], in_2[21]);
  not not_51 (not_29_out[22], in_2[22]);
  not not_52 (not_29_out[23], in_2[23]);
  not not_53 (not_29_out[24], in_2[24]);
  not not_54 (not_29_out[25], in_2[25]);
  not not_55 (not_29_out[26], in_2[26]);
  not not_56 (not_29_out[27], in_2[27]);
  not not_57 (not_29_out[28], in_2[28]);
  Multiplexer #(.width(29), .enable("false")) multiplexer_1 (
    .in0(n29bit_alu_1_out_4), .in1({in_1[28], not_1_out}), .out(multiplexer_1_out), .sel(xor_1_out));
  Multiplexer #(.width(29), .enable("false")) multiplexer_2 (
    .in0(in_1), .in1(multiplexer_1_out), .out(out_3), .sel(in_1[28]));
  _29bit_ALU u_29bit_alu_1 (
    .Control(2'b10), .in_2({in_1[28], not_1_out}), .in_3(29'h1), .out_4(n29bit_alu_1_out_4));  // open: Flags
  _29bit_ALU u_29bit_alu_2 (
    .Control(2'b10), .in_2(not_29_out), .in_3(29'h1), .out_4(n29bit_alu_2_out_4));  // open: Flags
  Multiplexer #(.width(29), .enable("false")) multiplexer_3 (
    .in0(in_2), .in1(n29bit_alu_2_out_4), .out(out_4), .sel(in_1[28]));
  xor xor_1 (xor_1_out, n29bit_alu_2_out_4[28], in_2[28]);
endmodule
