// Logisim project Traffic light v2.circ as structural Verilog: 1 circuit, main circuit main
module main (
  input  Set_it_to_1,
  input  in_2
);

  wire and_1_out, and_2_out, and_3_out, and_4_out, and_5_out, and_6_out, clock_1_out, d_ff_1_q, d_ff_2_q,
       d_ff_3_q, d_ff_4_q, d_ff_5_q, d_ff_6_q, d_ff_7_q, d_ff_8_q, j_k_ff_1_q, j_k_ff_1_qn, j_k_ff_2_q,
       j_k_ff_2_qn, j_k_ff_3_q, j_k_ff_3_qn, not_1_out, not_2_out, or_1_out, or_2_out, or_3_out, or_4_out,
       or_5_out, or_6_out;

  and and_1 (and_1_out, j_k_ff_2_q, j_k_ff_3_q);
  or or_1 (or_1_out, j_k_ff_3_q, j_k_ff_2_q);
  Clock clock_1 (.out(clock_1_out));
  J_K_Flip_Flop #(.trigger("falling")) j_k_ff_1 (
    .J(and_1_out), .clk(or_6_out), .K(or_1_out), .Q(j_k_ff_1_q), .Qn(j_k_ff_1_qn), .reset(in_2));  // open: preset, en
  and and_2 (and_2_out, j_k_ff_3_q, j_k_ff_1_qn);
  or or_2 (or_2_out, j_k_ff_3_q, j_k_ff_1_q);
  D_Flip_Flop #(.trigger("falling")) d_ff_1 (
    .clk(clock_1_out), .D(d_ff_8_q), .Q(d_ff_1_q), .preset(in_2));  // open: Qn, en, reset
  J_K_Flip_Flop #(.trigger("falling")) j_k_ff_2 (
    .J(and_2_out), .clk(or_6_out), .K(or_2_out), .Q(j_k_ff_2_q), .Qn(j_k_ff_2_qn), .reset(in_2));  // open: preset, en
  D_Flip_Flop d_ff_2 (.clk(clock_1_out), .D(d_ff_1_q), .Q(d_ff_2_q), .reset(in_2));  // open: Qn, preset, en
  or or_3 (or_3_out, j_k_ff_2_qn, j_k_ff_1_qn);
  D_Flip_Flop #(.trigger("falling")) d_ff_3 (
    .clk(clock_1_out), .D(d_ff_2_q), .Q(d_ff_3_q), .reset(in_2));  // open: Qn, preset, en
  J_K_Flip_Flop #(.trigger("falling")) j_k_ff_3 (
    .J(or_3_out), .clk(or_6_out), .K(Set_it_to_1), .Q(j_k_ff_3_q), .Qn(j_k_ff_3_qn), .reset(in_2));  // open: preset, en
  D_Flip_Flop #(.trigger("falling")) d_ff_4 (
    .clk(clock_1_out), .D(d_ff_3_q), .Q(d_ff_4_q), .reset(in_2));  // open: Qn, preset, en
  and and_3 (and_3_out, j_k_ff_1_q, j_k_ff_2_qn, j_k_ff_3_qn);
  and and_4 (and_4_out, j_k_ff_1_q, j_k_ff_3_q);
  and and_5 (and_5_out, j_k_ff_1_qn, j_k_ff_2_qn, j_k_ff_3_q);
  and and_6 (and_6_out, j_k_ff_1_qn, j_k_ff_2_q, j_k_ff_3_qn);
  D_Flip_Flop #(.trigger("falling")) d_ff_5 (
    .clk(clock_1_out), .D(d_ff_4_q), .Q(d_ff_5_q), .reset(in_2));  // open: Qn, preset, en
  LED led_1 (.in(and_3_out));
  or or_4 (or_4_out, and_3_out, and_4_out);
  or or_5 (or_5_out, and_5_out, and_6_out);
  D_Flip_Flop #(.trigger("falling")) d_ff_6 (
    .clk(clock_1_out), .D(d_ff_5_q), .Q(d_ff_6_q), .reset(in_2));  // open: Qn, preset, en
  LED led_2 (.in(not_1_out));
  LED led_3 (.in(and_4_out));
  not not_1 (not_1_out, or_4_out);
  LED led_4 (.in(and_5_out));
  not not_2 (not_2_out, or_5_out);
  D_Flip_Flop #(.trigger("falling")) d_ff_7 (
    .clk(clock_1_out), .D(d_ff_6_q), .Q(d_ff_7_q), .reset(in_2));  // open: Qn, preset, en
  LED led_5 (.in(not_2_out));
  LED led_6 (.in(and_6_out));
  D_Flip_Flop #(.trigger("falling")) d_ff_8 (
    .clk(clock_1_out), .D(d_ff_7_q), .Q(d_ff_8_q), .reset(in_2));  // open: Qn, preset, en
  or or_6 (or_6_out, d_ff_6_q, d_ff_2_q, d_ff_8_q);

  // Notes on the sheet:
  //   Click twice (0->1->0)
endmodule
