// Logisim project UpDownRippleCounter.circ as structural Verilog: 1 circuit, main circuit main
module main (
  input  in_1,
  input  in_2,
  output out_3,
  output out_4,
  output out_5
);

  wire and_1_out, and_2_out, and_3_out, and_4_out, clock_1_out, not_1_out, not_2_out, not_3_out, or_1_out,
       or_2_out;

  not not_1 (not_1_out, in_1);
  not not_2 (not_2_out, out_5);
  Clock clock_1 (.out(clock_1_out));
  and and_1 (and_1_out, not_1_out, out_5);
  and and_2 (and_2_out, in_1, not_2_out);
  or or_1 (or_1_out, and_1_out, and_2_out);
  T_Flip_Flop #(.trigger("falling")) t_ff_1 (.clk(clock_1_out), .T(in_2), .Q(out_5));  // open: Qn, preset, reset, en
  not not_3 (not_3_out, out_4);
  and and_3 (and_3_out, not_1_out, out_4);
  and and_4 (and_4_out, in_1, not_3_out);
  T_Flip_Flop #(.trigger("falling")) t_ff_2 (.clk(or_1_out), .T(in_2), .Q(out_4));  // open: Qn, preset, reset, en
  or or_2 (or_2_out, and_3_out, and_4_out);
  T_Flip_Flop #(.trigger("falling")) t_ff_3 (.clk(or_2_out), .T(in_2), .Q(out_3));  // open: Qn, preset, reset, en
endmodule
