// Logisim project adder-subtractor.circ as structural Verilog: 2 circuits, main circuit main
module main (
  input  in_1,
  input  in_2,
  input  in_3,
  input  in_4,
  input  in_5,
  input  in_6,
  input  in_7,
  input  in_8,
  input  in_9,
  output out_10,
  output out_11,
  output out_12,
  output out_13,
  output out_14
);

  wire and_1_out, and_2_out, and_3_out, and_4_out, and_5_out, and_6_out, and_7_out, and_8_out, and_9_out,
       and_10_out, and_11_out, and_12_out, or_1_out, or_2_out, or_3_out, xor_1_out, xor_2_out, xor_3_out,
       xor_4_out, xor_5_out, xor_6_out, xor_7_out, xor_8_out, xor_9_out, xor_10_out, xor_11_out, xor_12_out,
       xor_13_out, xor_14_out;

  and and_1 (and_1_out, xor_14_out, in_9);
  xor xor_1 (xor_1_out, xor_12_out, in_8);
  and and_2 (and_2_out, and_1_out, xor_1_out, xor_2_out);
  fa fa_1 (.in_1(in_6), .b(xor_11_out), .cin(or_1_out), .cout(out_14), .s(out_10));
  xor xor_2 (xor_2_out, xor_13_out, in_7);
  or or_1 (or_1_out, and_2_out, and_3_out, and_9_out, and_7_out);
  xor xor_3 (xor_3_out, xor_14_out, in_9);
  xor xor_4 (xor_4_out, xor_12_out, in_8);
  and and_3 (and_3_out, in_1, xor_4_out, xor_3_out, xor_8_out);
  xor xor_5 (xor_5_out, xor_12_out, in_8);
  xor xor_6 (xor_6_out, xor_14_out, in_9);
  and and_4 (and_4_out, xor_6_out, xor_5_out, in_1);
  xor xor_7 (xor_7_out, xor_13_out, in_7);
  xor xor_8 (xor_8_out, xor_13_out, in_7);
  fa fa_2 (.in_1(in_7), .b(xor_13_out), .cin(or_2_out), .s(out_11));  // open: cout
  and and_5 (and_5_out, xor_14_out, in_9);
  xor xor_9 (xor_9_out, xor_12_out, in_8);
  and and_6 (and_6_out, and_5_out, xor_9_out);
  and and_7 (and_7_out, xor_13_out, in_7);
  and and_8 (and_8_out, xor_12_out, in_8);
  and and_9 (and_9_out, xor_7_out, and_8_out);
  xor xor_10 (xor_10_out, xor_14_out, in_9);
  and and_10 (and_10_out, in_1, xor_10_out);
  and and_11 (and_11_out, xor_12_out, in_8);
  or or_2 (or_2_out, and_6_out, and_4_out, and_11_out);
  fa fa_3 (.in_1(in_8), .b(xor_12_out), .cin(or_3_out), .s(out_12));  // open: cout
  xor xor_11 (xor_11_out, in_1, in_2);
  and and_12 (and_12_out, xor_14_out, in_9);
  or or_3 (or_3_out, and_10_out, and_12_out);
  xor xor_12 (xor_12_out, in_1, in_4);
  xor xor_13 (xor_13_out, in_1, in_3);
  xor xor_14 (xor_14_out, in_1, in_5);
  fa fa_4 (.in_1(in_9), .b(xor_14_out), .cin(in_1), .s(out_13));  // open: cout
endmodule

module fa (
  input  in_1,
  input  b,
  input  cin,
  output cout,
  output s
);

  wire and_1_out, and_2_out, and_3_out, and_4_out, and_5_out, and_6_out, and_7_out, not_1_out, not_2_out,
       not_3_out, not_4_out, not_5_out, not_6_out;

  and and_1 (and_1_out, b, cin);
  and and_2 (and_2_out, in_1, cin);
  and and_3 (and_3_out, in_1, b);
  not not_1 (not_1_out, in_1);
  not not_2 (not_2_out, b);
  not not_3 (not_3_out, in_1);
  not not_4 (not_4_out, cin);
  not not_5 (not_5_out, b);
  not not_6 (not_6_out, cin);
  or or_1 (cout, and_1_out, and_2_out, and_3_out);
  and and_4 (and_4_out, not_1_out, not_2_out, cin);
  and and_5 (and_5_out, not_3_out, b, not_4_out);
  and and_6 (and_6_out, in_1, not_5_out, not_6_out);
  and and_7 (and_7_out, in_1, b, cin);
  or or_2 (s, and_4_out, and_5_out, and_6_out, and_7_out);
endmodule
