// Logisim project async_roll.circ as structural Verilog: 3 circuits, main circuit main
module main (
  input  in_1,
  input  in_2
);

  wire and_1_out, clock_1_out, n7seg_1_a_2, n7seg_1_b_2, n7seg_1_c_2, n7seg_1_d_2, n7seg_1_e, n7seg_1_f,
       n7seg_1_g, roll_1_x, roll_1_y, roll_1_z, t_ff_1_q, t_ff_2_q, t_ff_3_q;

  Clock clock_1 (.out(clock_1_out));
  T_Flip_Flop #(.trigger("falling")) t_ff_1 (
    .clk(clock_1_out), .T(in_2), .Q(t_ff_1_q), .reset(and_1_out));  // open: Qn, preset, en
  and and_1 (and_1_out, t_ff_1_q, t_ff_2_q, t_ff_3_q);
  T_Flip_Flop #(.trigger("falling")) t_ff_2 (
    .clk(t_ff_1_q), .T(in_2), .Q(t_ff_2_q), .reset(and_1_out));  // open: Qn, preset, en
  roll roll_1 (.a(t_ff_3_q), .b(t_ff_2_q), .c(t_ff_1_q), .x(roll_1_x), .y(roll_1_y), .z(roll_1_z));
  T_Flip_Flop #(.trigger("falling")) t_ff_3 (
    .clk(t_ff_2_q), .T(in_2), .Q(t_ff_3_q), .reset(and_1_out));  // open: Qn, preset, en
  _7seg u_7seg_1 (
    .a(in_1), .b(roll_1_x), .c(roll_1_y), .d(roll_1_z), .a_2(n7seg_1_a_2), .b_2(n7seg_1_b_2),
    .c_2(n7seg_1_c_2), .d_2(n7seg_1_d_2), .e(n7seg_1_e), .f(n7seg_1_f), .g(n7seg_1_g));
  _7_Segment_Display u_7_segment_display_1 (
    .g(n7seg_1_g), .f(n7seg_1_f), .a(n7seg_1_a_2), .b(n7seg_1_b_2), .e(n7seg_1_d_2), .d(n7seg_1_e),
    .c(n7seg_1_c_2));  // open: dp
endmodule

module _7seg (
  input  a,
  input  b,
  input  c,
  input  d,
  output a_2,
  output b_2,
  output c_2,
  output d_2,
  output e,
  output f,
  output g
);

  wire and_1_out, and_2_out, and_3_out, and_4_out, and_5_out, and_6_out, and_7_out, and_8_out, and_9_out,
       and_10_out, and_11_out, and_12_out, and_13_out, and_14_out, and_15_out, and_16_out, not_1_out,
       not_2_out, not_3_out, not_4_out, not_5_out, not_6_out, not_7_out, not_8_out, not_9_out, not_10_out,
       not_11_out, not_12_out, not_13_out, not_14_out, not_15_out, not_16_out, not_17_out, not_18_out,
       not_19_out, not_20_out, not_21_out;

  not not_1 (not_1_out, b);
  and and_1 (and_1_out, not_1_out, not_2_out);
  not not_2 (not_2_out, d);
  and and_2 (and_2_out, b, d);
  not not_3 (not_3_out, b);
  not not_4 (not_4_out, c);
  and and_3 (and_3_out, not_4_out, not_5_out);
  not not_5 (not_5_out, d);
  and and_4 (and_4_out, c, d);
  not not_6 (not_6_out, c);
  or or_1 (c_2, not_6_out, d, b);
  not not_7 (not_7_out, b);
  and and_5 (and_5_out, not_7_out, not_8_out);
  not not_8 (not_8_out, d);
  not not_9 (not_9_out, b);
  and and_6 (and_6_out, not_9_out, c);
  and and_7 (and_7_out, c, not_10_out);
  not not_10 (not_10_out, d);
  and and_8 (and_8_out, b, not_11_out, d);
  not not_11 (not_11_out, c);
  not not_12 (not_12_out, b);
  and and_9 (and_9_out, not_12_out, not_13_out);
  not not_13 (not_13_out, d);
  and and_10 (and_10_out, c, not_14_out);
  not not_14 (not_14_out, d);
  not not_15 (not_15_out, c);
  and and_11 (and_11_out, not_15_out, not_16_out);
  not not_16 (not_16_out, d);
  and and_12 (and_12_out, b, not_17_out);
  not not_17 (not_17_out, c);
  and and_13 (and_13_out, b, not_18_out);
  not not_18 (not_18_out, d);
  not not_19 (not_19_out, b);
  and and_14 (and_14_out, not_19_out, c);
  and and_15 (and_15_out, b, not_20_out);
  not not_20 (not_20_out, c);
  and and_16 (and_16_out, b, not_21_out);
  not not_21 (not_21_out, d);
  or or_2 (a_2, and_1_out, c, and_2_out, a);
  or or_3 (b_2, not_3_out, and_3_out, and_4_out);
  or or_4 (d_2, and_5_out, and_6_out, and_7_out, and_8_out, a);
  or or_5 (e, and_9_out, and_10_out);
  or or_6 (f, and_11_out, and_12_out, and_13_out, a);
  or or_7 (g, and_14_out, and_15_out, and_16_out, a);
endmodule

module roll (
  input  a,
  input  b,
  input  c,
  output x,
  output y,
  output z
);

  wire and_1_out, and_2_out, and_3_out, and_4_out, and_5_out, not_1_out, not_2_out, not_3_out, not_4_out,
       not_5_out, not_6_out;

  not not_1 (not_1_out, a);
  not not_2 (not_2_out, c);
  not not_3 (not_3_out, a);
  not not_4 (not_4_out, b);
  not not_5 (not_5_out, a);
  not not_6 (not_6_out, a);
  and and_1 (and_1_out, not_1_out, b, c);
  and and_2 (and_2_out, a, b, not_2_out);
  and and_3 (and_3_out, not_3_out, not_4_out);
  and and_4 (and_4_out, not_5_out, c);
  and and_5 (and_5_out, a, b);
  and and_6 (z, not_6_out, b, c);
  or or_1 (x, and_1_out, and_2_out);
  or or_2 (y, and_3_out, and_4_out, and_5_out);
endmodule
