// Logisim project jk_async.circ as structural Verilog: 1 circuit, main circuit main
module main (
  input  in_1,
  input  in_2,
  output out_3,
  output out_4,
  output out_5,
  output out_6
);

  wire and_1_out, clock_1_out, j_k_ff_4_qn;

  Clock clock_1 (.out(clock_1_out));
  J_K_Flip_Flop #(.trigger("falling")) j_k_ff_1 (
    .J(in_2), .clk(clock_1_out), .K(in_2), .Q(out_6), .reset(in_1));  // open: Qn, preset, en
  J_K_Flip_Flop #(.trigger("falling")) j_k_ff_2 (
    .J(j_k_ff_4_qn), .clk(out_6), .K(in_2), .Q(out_5), .reset(in_1));  // open: Qn, preset, en
  J_K_Flip_Flop #(.trigger("falling")) j_k_ff_3 (
    .J(in_2), .clk(out_5), .K(in_2), .Q(out_4), .reset(in_1));  // open: Qn, preset, en
  and and_1 (and_1_out, out_5, out_4);
  J_K_Flip_Flop #(.trigger("falling")) j_k_ff_4 (
    .J(and_1_out), .clk(out_6), .K(in_2), .Q(out_3), .Qn(j_k_ff_4_qn), .reset(in_1));  // open: preset, en
endmodule
